// Logisim project lklk.circ as structural Verilog: 6 circuits, main circuit main
module main (
  input  in_1,
  input  in_2,
  input  in_3,
  input  in_4,
  input  in_5,
  output [3:0] out_6
);

  wire clock_1_out;

  Clock clock_1 (.out(clock_1_out));
  registro4bits registro4bits_1 (
    .i0(in_1), .i1(in_2), .i2(in_3), .i3(in_4), .load(in_5), .clk(clock_1_out), .out_8(out_6[0]),
    .out_9(out_6[1]), .out_10(out_6[2]), .out_11(out_6[3]));  // open: inc
  birideccional birideccional_1 ();  // open: load, clk, read, out_4, out_5, out_6, out_7
  registro4bits registro4bits_2 ();  // open: i0, i1, i2, i3, load, clk, inc, out_8, out_9, out_10, out_11
endmodule

module registro4bits (
  input  i0,
  input  i1,
  input  i2,
  input  i3,
  input  load,
  input  clk,
  input  inc,
  output out_8,
  output out_9,
  output out_10,
  output out_11
);

  wire [3:0] controlled_buffer_1_out, incrementador_4_1_p2, multiplexer_1_out;

  assign controlled_buffer_1_out[0] = load ? i0 : 1'bz;  // Controlled_Buffer controlled_buffer_1
  assign controlled_buffer_1_out[1] = load ? i1 : 1'bz;  // Controlled_Buffer controlled_buffer_2
  assign controlled_buffer_1_out[2] = load ? i2 : 1'bz;  // Controlled_Buffer controlled_buffer_3
  assign controlled_buffer_1_out[3] = load ? i3 : 1'bz;  // Controlled_Buffer controlled_buffer_4
  Multiplexer #(.width(4)) multiplexer_1 (
    .in0(controlled_buffer_1_out), .in1(incrementador_4_1_p2), .out(multiplexer_1_out), .sel(inc));
  D_Flip_Flop d_ff_1 (.D(multiplexer_1_out[0]), .clk(clk), .Q(out_8));  // open: Qn, preset, reset
  D_Flip_Flop d_ff_2 (.D(multiplexer_1_out[1]), .clk(clk), .Q(out_9));  // open: Qn, preset, reset
  D_Flip_Flop d_ff_3 (.D(multiplexer_1_out[2]), .clk(clk), .Q(out_10));  // open: Qn, preset, reset
  D_Flip_Flop d_ff_4 (.D(multiplexer_1_out[3]), .clk(clk), .Q(out_11));  // open: Qn, preset, reset
  // incrementador_4 incrementador_4_1: pin names not known; wires that end beside it: {out_11, out_10, out_9, out_8}, incrementador_4_1_p2
endmodule

module birideccional (
  input  load,
  input  clk,
  input  read,
  output out_4,
  output out_5,
  output out_6,
  output out_7
);

  wire registro4bits_1_out_8, registro4bits_1_out_9, registro4bits_1_out_10, registro4bits_1_out_11;

  registro4bits registro4bits_1 (
    .i0(registro4bits_1_out_8), .i1(registro4bits_1_out_9), .i2(registro4bits_1_out_10),
    .i3(registro4bits_1_out_11), .load(load), .clk(clk), .out_8(registro4bits_1_out_8),
    .out_9(registro4bits_1_out_9), .out_10(registro4bits_1_out_10), .out_11(registro4bits_1_out_11));  // open: inc
  assign out_5 = read ? registro4bits_1_out_9 : 1'bz;  // Controlled_Buffer controlled_buffer_1
  assign out_6 = read ? registro4bits_1_out_10 : 1'bz;  // Controlled_Buffer controlled_buffer_2
  assign out_7 = read ? registro4bits_1_out_11 : 1'bz;  // Controlled_Buffer controlled_buffer_3
  assign out_4 = read ? registro4bits_1_out_8 : 1'bz;  // Controlled_Buffer controlled_buffer_4
endmodule

module extensorDeSigno (
  input  I0,
  input  i1,
  input  i2,
  input  i3,
  input  load,
  input  clk,
  input  ext,
  output [3:0] out_8
);

  wire [3:0] complementoa24bits_1_out_5, registro4bits_1_out_8;

  registro4bits registro4bits_1 (
    .i0(I0), .i1(i1), .i2(i2), .i3(i3), .load(load), .clk(clk), .out_8(registro4bits_1_out_8[0]),
    .out_9(registro4bits_1_out_8[1]), .out_10(registro4bits_1_out_8[2]), .out_11(registro4bits_1_out_8[3]));  // open: inc
  complementoA24Bits complementoa24bits_1 (
    .in_1(registro4bits_1_out_8[3]), .in_2(registro4bits_1_out_8[2]), .in_3(1'b0), .in_4(1'b0),
    .out_5(complementoa24bits_1_out_5));
  Multiplexer #(.width(4)) multiplexer_1 (
    .in0(registro4bits_1_out_8), .in1(complementoa24bits_1_out_5), .out(out_8), .sel(ext));
endmodule

module complementoA24Bits (
  input  in_1,
  input  in_2,
  input  in_3,
  input  in_4,
  output [3:0] out_5
);

  // inversor_4 inversor_4_1: pin names not known; wires that end beside it: {in_4, in_3, in_2, in_1}, 1'b1
  // incrementador_4 incrementador_4_1: pin names not known; wires that end beside it: out_5
endmodule

module DesplazadorAIzq (
  input  I0,
  input  i1,
  input  i2,
  input  i3,
  input  load,
  input  clk,
  input  shl,
  output [3:0] out_8
);

  wire [3:0] adder_1_out, registro4bits_1_out_8;

  registro4bits registro4bits_1 (
    .i0(I0), .i1(i1), .i2(i2), .i3(i3), .load(load), .clk(clk), .out_8(registro4bits_1_out_8[0]),
    .out_9(registro4bits_1_out_8[1]), .out_10(registro4bits_1_out_8[2]), .out_11(registro4bits_1_out_8[3]));  // open: inc
  Adder #(.width(4)) adder_1 (
    .a(registro4bits_1_out_8), .b(registro4bits_1_out_8), .out(adder_1_out));  // open: cin, cout
  Multiplexer #(.width(4)) multiplexer_1 (.in0(registro4bits_1_out_8), .in1(adder_1_out), .out(out_8), .sel(shl));
endmodule
